# Fritzing sketch TowerClock (saved by Fritzing 0.9.4)
breadboards: 1

parts:
  Bauteil1 = LED Strip
  Bauteil2 = Arduino Nano (Rev3.0)
  Bauteil3 = Real Time Clock Module - DS1307 RTC Breakout Board
  Button = Momentary Switch [package=ksa_sealed_tac_switch]
  5V_Power_Supply = Power plug
  R1 = Resistor [tolerance=±5% resistance=27k package=THT]
  R3 = Resistor [tolerance=±5% resistance=1.96k package=THT]
  Photoresistor = PHOTOCELL [package=photocell]

nets:
  5V: Bauteil1.5V, Bauteil2.VIN, Bauteil3.5V, Button.3, 5V_Power_Supply.VCC, Photoresistor.P$1
  N1: Bauteil1.Din, Bauteil2.D3
  GND: Bauteil1.GND, Bauteil2.GND, Bauteil3.GND, 5V_Power_Supply.GND, R1.Pin_1, R3.Pin_1
  N2: Bauteil2.D2, Button.2
  N3: Bauteil2.A5, Bauteil3.SCL
  N4: Bauteil2.A4, Bauteil3.SDA
  N5: Bauteil2.A2, R3.Pin_0, Photoresistor.P$2
  N6: Button.1, R1.Pin_0

custom parts:
  LED Strip: LED Strip with LEDs like WS2811
